// Logisim project Tarea3_2020735956.circ as structural Verilog: 4 circuits, main circuit main
module main (
  input  [1:0] in_1,
  input  [7:0] in_2,
  output out_3,
  output [7:0] Registro_1,
  output [7:0] Registro_2,
  output [7:0] Registro_3,
  output DONT_CARE,
  output DONT_CARE_2,
  output DONT_CARE_3,
  output DONT_CARE_4,
  output DONT_CARE_5,
  output DONT_CARE_6
);

  wire clock_1_out, demultiplexer_1_out0, demultiplexer_1_out1, demultiplexer_1_out2;
  wire [1:0] demultiplexer_2_out3;
  wire [7:0] demultiplexer_2_out0, demultiplexer_2_out1, demultiplexer_2_out2, multiplexer_1_out;

  Demultiplexer #(.select(2), .enable("false")) demultiplexer_1 (
    .out0(demultiplexer_1_out0), .out1(demultiplexer_1_out1), .out2(demultiplexer_1_out2), .out3(out_3),
    .in(clock_1_out), .sel(in_1));
  Clock clock_1 (.out(clock_1_out));
  Demultiplexer #(.select(2), .width(8), .enable("false")) demultiplexer_2 (
    .out0(demultiplexer_2_out0), .out1(demultiplexer_2_out1), .out2(demultiplexer_2_out2),
    .out3({DONT_CARE_6, DONT_CARE_5, DONT_CARE_4, DONT_CARE_3, DONT_CARE_2, DONT_CARE, demultiplexer_2_out3}),
    .in(in_2), .sel(in_1));
  Register register_1 (.D(demultiplexer_2_out0), .Clk(demultiplexer_1_out0), .out_3(Registro_1));
  Register register_2 (.D(demultiplexer_2_out1), .Clk(demultiplexer_1_out1), .out_3(Registro_2));
  Register register_3 (.D(demultiplexer_2_out2), .Clk(demultiplexer_1_out2), .out_3(Registro_3));
  LED led_1 (.in(multiplexer_1_out[7]));
  Multiplexer #(.select(2), .width(8), .enable("false")) multiplexer_1 (
    .in1(Registro_1), .in2(Registro_2), .in3(Registro_3), .out(multiplexer_1_out), .sel(demultiplexer_2_out3));  // open: in0
  LED led_2 (.in(multiplexer_1_out[5]));
  LED led_3 (.in(multiplexer_1_out[4]));
  LED led_4 (.in(multiplexer_1_out[6]));
  LED led_5 (.in(multiplexer_1_out[3]));
  LED led_6 (.in(multiplexer_1_out[0]));
  LED led_7 (.in(multiplexer_1_out[2]));
  LED led_8 (.in(multiplexer_1_out[1]));
endmodule

module SR_Latch__Active_Low (
  input  nS,
  input  nR,
  output Q
);

  wire nand_2_out;

  nand nand_1 (Q, nS, nand_2_out);
  nand nand_2 (nand_2_out, Q, nR);
endmodule

module D_Latch__Active_Low (
  input  D,
  input  Clk,
  output Out
);

  wire nand_1_out, nand_2_out, not_1_out;

  not not_1 (not_1_out, D);
  nand nand_1 (nand_1_out, D, Clk);
  nand nand_2 (nand_2_out, Clk, not_1_out);
  SR_Latch__Active_Low sr_latch_active_low_1 (.nS(nand_1_out), .nR(nand_2_out), .Q(Out));
endmodule

module Register (
  input  [7:0] D,
  input  Clk,
  output [7:0] out_3
);

  D_Latch__Active_Low d_latch_active_low_1 (.D(D[7]), .Clk(Clk), .Out(out_3[7]));
  D_Latch__Active_Low d_latch_active_low_2 (.D(D[6]), .Clk(Clk), .Out(out_3[6]));
  D_Latch__Active_Low d_latch_active_low_3 (.D(D[5]), .Clk(Clk), .Out(out_3[5]));
  D_Latch__Active_Low d_latch_active_low_4 (.D(D[4]), .Clk(Clk), .Out(out_3[4]));
  D_Latch__Active_Low d_latch_active_low_5 (.D(D[3]), .Clk(Clk), .Out(out_3[3]));
  D_Latch__Active_Low d_latch_active_low_6 (.D(D[2]), .Clk(Clk), .Out(out_3[2]));
  D_Latch__Active_Low d_latch_active_low_7 (.D(D[1]), .Clk(Clk), .Out(out_3[1]));
  D_Latch__Active_Low d_latch_active_low_8 (.D(D[0]), .Clk(Clk), .Out(out_3[0]));
endmodule
